// Digital circuit 8bit_cpu.dig as structural Verilog
module _8bit_cpu (
  input  CLK,
  output [7:0] out_2,
  output [7:0] out_3,
  output [7:0] out_4
);

  wire IR_en, MAR_en, ORI_out, PC_inc, T4, T5, T6;
  wire [7:0] _8bit_adder_subtractor_1_s, driver_1_out, driver_2_out, PC_q;

  _8bit_adder_subtractor _8bit_adder_subtractor_1 (
    .CTR(1'b0), .A(PC_q), .B(8'h1), .S(_8bit_adder_subtractor_1_s));  // open: _2
  assign driver_1_out = PC_inc ? _8bit_adder_subtractor_1_s : 8'bz;  // Driver driver_1
  Register #(.Bits(8)) PC (.D(driver_1_out), .C(CLK), .en(PC_inc), .Q(PC_q));
  Button ORI (.out(ORI_out));
  assign driver_2_out = MAR_en ? PC_q : 8'bz;  // Driver driver_2
  D_FF_AS d_ff_as_1 (.Set(ORI_out), .D(T6), .C(CLK), .Clr(ORI_out), .Q(MAR_en));  // open: nQ
  D_FF_AS d_ff_as_2 (.Set(1'b0), .D(MAR_en), .C(CLK), .Clr(ORI_out), .Q(IR_en));  // open: nQ
  // And and_1 is placed but not wired
  Register #(.Bits(8)) IR (.D(driver_2_out), .C(CLK), .en(IR_en), .Q(out_3));
  D_FF_AS d_ff_as_3 (.Set(1'b0), .D(IR_en), .C(CLK), .Clr(ORI_out), .Q(PC_inc));  // open: nQ
  D_FF_AS d_ff_as_4 (.Set(1'b0), .D(PC_inc), .C(CLK), .Clr(ORI_out), .Q(T4));  // open: nQ
  Register #(.Bits(8)) MAR (.C(CLK), .en(MAR_en), .Q(out_4));  // open: D
  D_FF_AS d_ff_as_5 (.Set(1'b0), .D(T4), .C(CLK), .Clr(ORI_out), .Q(T5));  // open: nQ
  ROM #(.AddrBits(8), .Bits(8)) INSTRUCTIONS (.A(out_4), .sel(IR_en), .D(driver_2_out));
  ROM #(.AddrBits(8), .Bits(8)) OPERANDS (.A(out_4), .sel(1'b0), .D(out_2));
  D_FF_AS d_ff_as_6 (.Set(1'b0), .D(T5), .C(CLK), .Clr(ORI_out), .Q(T6));  // open: nQ

  // Other names for the same wires on the sheet: PC_en = MAR_en; T1 = MAR_en; ROM_IN = IR_en; T2 = IR_en; T3 = PC_inc

  // Notes on the sheet:
  //   contents of INSTRUCTIONS (hex, n*v repeats v):
  //   7,1,2,3
  //   contents of OPERANDS (hex, n*v repeats v):
  //   6,2,4
endmodule
